# Fritzing sketch Lesson03b-switch-button (saved by Fritzing 0.9.6b)
breadboards: 1

parts:
  Mod1 = Raspberry Pi Pico W
  S1 = Toggle Switch [package=THT]
  LED1 = LED - 3mm [color="Red (633nm)" current=0.030 package="3 mm [THT]"]
  R1 = Resistor [tolerance=±5% resistance=220 package="0603 [SMD]"]
  LED2 = LED - 3mm [color="Red (633nm)" current=0.030 package="3 mm [THT]"]
  R2 = Resistor [tolerance=±5% resistance=220 package="0603 [SMD]"]
  S2 = Pushbutton [package="[THT]"]
  R3 = Resistor [tolerance=±5% resistance=10000 package="0805 [SMD]"]
  R4 = Resistor [tolerance=±5% resistance=10000 package="0805 [SMD]"]

nets:
  N1: Mod1.pin_3, Mod1.pin_8, Mod1.pin_13, Mod1.pin_18, Mod1.pin_23, Mod1.pin_28, Mod1.pin_33, Mod1.pin_38, Mod1.pin_42, S1.L1, R1.Pin_1, R2.Pin_1, S2.Pin_1, S2.Pin_2
  N2: Mod1.pin_19, LED2.anode
  N3: Mod1.pin_20, LED1.anode
  N4: Mod1.pin_21, S1.COM
  N5: Mod1.pin_22, R3.Pin_0
  N6: Mod1.pin_36, S1.L2, R4.Pin_1
  N7: LED1.cathode, R1.Pin_0
  N8: LED2.cathode, R2.Pin_0
  N9: S2.Pin_3, S2.Pin_4, R3.Pin_1, R4.Pin_0

custom parts:
  Raspberry Pi Pico W: Raspberry Pi Pico W. Based around the RP2040 microcontroller the Pico W is a low cost microcontroller device bringing Raspberry Pi quality, cost, and easy of use to the microcontroller space. The areas marked KEEPOUT in pcb silkscreen should not have traces running through them to avoid shorts on a soldered in module!
